# Fritzing sketch Dongle (saved by Fritzing 0.9.3b)

parts:
  ESP = ESP8266 WiFi Module
  Pro_Micro = SparkFun Pro Micro
  S1 = Pushbutton [package="[THT]"]
  S2 = Pushbutton [package="[THT]"]

nets:
  N1: ESP.RXD, Pro_Micro.TX0
  VCC: ESP.VCC, ESP.CH_PD, Pro_Micro.VCC
  N2: ESP.RST, S1.Pin_3
  GND: ESP.GND, Pro_Micro.GND, S1.Pin_1, S2.Pin_3, S2.Pin_4
  N3: ESP.TXD, Pro_Micro.RX1
  N4: Pro_Micro.RST, S2.Pin_2

custom parts:
  ESP8266 WiFi Module: Generic WiFi Module based on the ESP8266 with onboard PCB antenna and UART communications
  SparkFun Pro Micro: The Pro Micro is similar to the Pro Mini except with an ATmega32U4 on board. The USB transceiver inside the 32U4 allows us to add USB connectivity on-board and do away with bulky external USB interface. Based on: https://github.com/unorthodox-engineers/unorthodox-arduino/blob/master/Unorthodox/fritzing/parts/Pro%20Micro.fzpz
